# Fritzing sketch schema (saved by Fritzing 0.9.2b)
breadboards: 1

parts:
  S1 = Pushbutton [package="[THT]"]
  LCD1 = LCD screen
  U1 = NodeMCU V3.0
  U2 = Breadboard Power Supply [package=THT]
  R1 = Resistor [tolerance=±1% resistance=10k package="0805 [SMD]"]
  DHT1 = DHT11 Humitidy and Temperature Sensor
  LCM1602_IIC1 = LCM1602 IIC [part_number="LCM1602 IIC" chip_label="LCM1602 IIC" package="DIP (Dual Inline) [THT]"]
  R2 = Resistor [tolerance=±1% resistance=10k package="0805 [SMD]"]
  S2 = Pushbutton [package="[THT]"]
  R3 = Resistor [tolerance=±1% resistance=10k package="0805 [SMD]"]
  S3 = Pushbutton [package="[THT]"]

nets:
  N1: S1.Pin_1, U1.D1, R1.Pin_0
  VIN: S1.Pin_3, U1.Vin, U2.pin3, U2.pin4, DHT1.VDD, S2.Pin_3, S2.Pin_4, S3.Pin_3
  VSS: LCD1.VSS, LCM1602_IIC1.VSS
  VDD: LCD1.VDD, LCM1602_IIC1.VDD
  N2: LCD1.V0, LCM1602_IIC1.V0
  N3: LCD1.RS, LCM1602_IIC1.RS
  N4: LCD1.R/W, LCM1602_IIC1.RW
  N5: LCD1.E, LCM1602_IIC1.E
  N6: LCD1.DB0, LCM1602_IIC1.D0
  N7: LCD1.DB1, LCM1602_IIC1.D1
  N8: LCD1.DB2, LCM1602_IIC1.D2
  N9: LCD1.DB3, LCM1602_IIC1.D3
  N10: LCD1.DB4, LCM1602_IIC1.D4
  N11: LCD1.DB5, LCM1602_IIC1.D5
  N12: LCD1.DB6, LCM1602_IIC1.D6
  N13: LCD1.DB7, LCM1602_IIC1.D7
  N14: LCD1.LED+, LCM1602_IIC1.A
  N15: LCD1.LED-, LCM1602_IIC1.K
  N16: U1.D2, R2.Pin_0, S2.Pin_1
  N17: U1.D3, LCM1602_IIC1.SCL
  N18: U1.D4, LCM1602_IIC1.SDA
  GND: U1.GND, U2.pin1, U2.pin2, R1.Pin_1, DHT1.GND, R2.Pin_1, R3.Pin_1
  N19: U1.D6, R3.Pin_0, S3.Pin_1
  N20: U1.D7, DHT1.DATA
  N21: U2.pin5, U2.pin6, LCM1602_IIC1.GND
  N22: U2.pin7, U2.pin8, LCM1602_IIC1.VCC
  N23: LCM1602_IIC1.LED_A, LCM1602_IIC1.LED_B

custom parts:
  NodeMCU V3.0: ESP8266 based NodeMCU
  Breadboard Power Supply: Représentation Carte Breadboard Power Supply
  DHT11 Humitidy and Temperature Sensor: DHT11 Humidity and Temperature Sensor
  LCM1602 IIC: I2C-Module to use a 1602 or 2004 LCD on with the wire.h libory Serial LCD Modul
